# Fritzing sketch RPiFritzfzz (saved by Fritzing 0.8.7b)
breadboards: 1

parts:
  IC1 = Eleduino T-Cobbler [chip_label=IC package=Custom]  # not connected
  R1 = Resistor [tolerance=±5% resistance=220 package=THT]
  R2 = Resistor [tolerance=±5% resistance=220 package=THT]
  R3 = Resistor [tolerance=±5% resistance=220 package=THT]
  R4 = Resistor [tolerance=±5% resistance=220 package=THT]
  R5 = Resistor [tolerance=±5% resistance=220 package=THT]
  R6 = Resistor [tolerance=±5% resistance=220 package=THT]
  LED6 = LED - 5mm [color="Red (633nm)" package="5 mm [THT]"]
  LED5 = LED - 5mm [color="Yellow (595nm)" package="5 mm [THT]"]
  LED4 = LED - 5mm [color="Green (570nm)" package="5 mm [THT]"]
  LED_1 = LED - 5mm [color="Green (570nm)" package="5 mm [THT]"]
  LED2 = LED - 5mm [color="Yellow (595nm)" package="5 mm [THT]"]
  LED3 = LED - 5mm [color="Red (633nm)" package="5 mm [THT]"]

nets:
  N1: R1.Pin_0, LED5.cathode
  N2: R1.Pin_1, R2.Pin_1, R3.Pin_1, R4.Pin_1, R5.Pin_1
  N3: R2.Pin_0, LED_1.cathode
  N4: R3.Pin_0, LED6.cathode
  N5: R4.Pin_0, LED2.cathode
  N6: R5.Pin_0, LED4.cathode
  N7: R6.Pin_0, LED3.cathode

custom parts:
  Eleduino T-Cobbler: The Alvar and Hurriks T-Cobbler for use with the Raspberry Pi v2 Model B or v3 for bringout out the GPIO pins to a breadboard.
